# Fritzing sketch love-o-meter (saved by Fritzing 0.9.3b)
breadboards: 1

parts:
  Part1 = Arduino Uno (Rev3) - ICSP
  T1 = TMP36 Temperature Sensor [package="TO92 [THT]"]
  LED1 = LED - 3mm [color="Red (633nm)" package="3 mm [THT]"]
  LED2 = LED - 3mm [color="Red (633nm)" package="3 mm [THT]"]
  LED3 = LED - 3mm [color="Red (633nm)" package="3 mm [THT]"]

nets:
  N1: Part1.A0, T1.Vout
  N2: Part1.D2, LED3.cathode
  N3: Part1.D3_PWM, LED2.cathode
  N4: Part1.D4, LED1.cathode
  N5: Part1.5V, T1.+Vs
  GND: Part1.GND, T1.GND, LED1.anode, LED2.anode, LED3.anode
